# Fritzing sketch Fritzing_Layout (saved by Fritzing 0.9.9b)
perfboards: 1

parts:
  7404_Hex_Inverter = IC, DIP package, 16 pins [chip_label=IC]
  MIDI_Out = DIN-5 jack (MIDI) [package=THT]
  MIDI_In = DIN-5 jack (MIDI) [package=THT]
  R2 = Resistor [tolerance=±5% power=0.25 resistance=220 package=THT]
  4N35_Optocoupler = IC, DIP package, 6 pins [chip_label=IC]
  D1 = Rectifier Diode [part_number=1N914 package="300 mil [THT]"]
  J1_ESP32 = double row female pin header, 20 pins [form="♀ (female)"]
  J2_ESP32 = double row female pin header, 20 pins [form="♀ (female)"]
  R4 = Resistor [tolerance=±5% power=0.25 resistance=220 package=THT]
  R1 = Resistor [tolerance=±5% power=0.25 resistance=220 package=THT]
  R5 = Resistor [tolerance=±5% power=0.25 resistance=220 package=THT]
  R6 = Resistor [tolerance=±5% power=0.25 resistance=220 package=THT]
  R7 = Resistor [tolerance=±5% power=0.25 resistance=100 package=THT]
  R8 = Resistor [tolerance=±5% power=0.25 resistance=10 package=THT]
  R9 = Resistor [tolerance=±5% power=0.25 resistance=10 package=THT]

nets:
  N1: 7404_Hex_Inverter.pin1, J2_ESP32.pin9
  N2: 7404_Hex_Inverter.pin2, 7404_Hex_Inverter.pin3
  N3: 7404_Hex_Inverter.pin4, R1.Pin_1
  GND: 7404_Hex_Inverter.pin8, 4N35_Optocoupler.pin4, J2_ESP32.pin20
  5V: 7404_Hex_Inverter.pin16, R2.Pin_0, J1_ESP32.pin1, R5.Pin_0
  N4: MIDI_Out.5, R2.Pin_1
  N5: MIDI_Out.4, R1.Pin_0
  N6: MIDI_In.5, R4.Pin_1
  N7: MIDI_In.4, 4N35_Optocoupler.pin1, D1.cathode
  N8: 4N35_Optocoupler.pin2, D1.anode, R4.Pin_0
  N9: 4N35_Optocoupler.pin5, J2_ESP32.pin8, R8.Pin_1
  N10: R5.Pin_1, R6.Pin_0
  N11: R6.Pin_1, R7.Pin_0
  N12: R7.Pin_1, R9.Pin_0
  N13: R8.Pin_0, R9.Pin_1
